// Logisim project not_gate.circ as structural Verilog
module main (
  input  a,
  output y
);

  // not_gate not_gate_1: pin names not known; wires that end beside it: a, y
endmodule

module builtin_not (
  input  a,
  output y_ref
);

  not not_1 (y_ref, a);
endmodule

// VHDL entity not_gate, as the project stores it:
library ieee;
use ieee.std_logic_1164.all;

entity not_gate is
  port (
    a : in  std_logic;
    y : out std_logic
  );
end not_gate;

architecture behavioral of not_gate is
begin
  y <= not a;
end behavioral;
